// Logisim project muxrisccore.circ as structural Verilog: 1 circuit, main circuit main
module main (
);

  wire and_1_out, and_2_out, and_3_out, bitselector_1_out, bitselector_5_out, clock_1_out, clock_2_out,
       clock_3_out, clock_4_out, clock_5_out, clock_6_out, clock_7_out, clock_8_out, clock_9_out,
       clock_10_out, clock_11_out, clock_12_out, comparator_1_eq, comparator_3_eq, comparator_4_eq,
       comparator_5_eq, comparator_6_eq, comparator_7_eq, comparator_8_eq, comparator_8_lt, comparator_9_eq,
       comparator_10_eq, comparator_11_eq, comparator_11_gt, comparator_12_eq, comparator_12_gt, counter_1_q,
       demultiplexer_1_out0, demultiplexer_1_out1, demultiplexer_1_out2, demultiplexer_1_out3,
       fpcomparator_1_p6, fpcomparator_1_p7, multiplexer_1_out, multiplexer_2_out, multiplexer_9_out,
       not_1_out, not_2_out, not_3_out, not_4_out, or_1_out, or_2_out, or_5_out, or_6_out, register_7_q,
       register_9_q;
  wire [1:0] counter_2_q, counter_3_q;
  wire [3:0] bitselector_2_out, bitselector_3_out, bitselector_4_out;
  wire [15:0] bitselector_6_out, bitselector_7_out, bitselector_8_out, counter_4_q, multiplexer_4_out,
       multiplexer_5_out, multiplexer_8_out;
  wire [63:0] fpcomparator_1_p4, multiplexer_3_out, multiplexer_6_out, multiplexer_10_out, or_3_out,
       or_4_out, ram_1_dout, register_1_q, register_2_q, register_3_q, register_4_q, register_5_q,
       register_6_q, register_8_q;

  Register #(.width(64)) register_1 (
    .D(multiplexer_3_out), .en(demultiplexer_1_out0), .clk(clock_1_out), .Q(register_1_q));  // open: clr
  Clock clock_1 (.out(clock_1_out));
  Register #(.trigger("falling"), .width(64)) register_2 (
    .D(ram_1_dout), .en(or_1_out), .clk(clock_2_out), .Q(register_2_q));  // open: clr
  or or_1 (or_1_out, or_5_out, comparator_1_eq);
  Comparator #(.width(64)) comparator_1 (.a({64{1'b0}}), .b(register_2_q), .eq(comparator_1_eq));  // open: gt, lt
  Clock clock_2 (.out(clock_2_out));
  BitSelector #(.width(64)) bitselector_1 (.in(register_2_q), .out(bitselector_1_out), .sel(6'b110100));
  Register #(.width(64)) register_3 (
    .D(multiplexer_3_out), .en(demultiplexer_1_out1), .clk(clock_3_out), .Q(register_3_q));  // open: clr
  Clock clock_3 (.out(clock_3_out));
  BitSelector #(.group(4), .width(64)) bitselector_2 (.in(register_2_q), .out(bitselector_2_out), .sel(4'b1110));
  BitSelector #(.group(4), .width(64)) bitselector_3 (.in(register_2_q), .out(bitselector_3_out), .sel(4'b0000));
  BitSelector #(.group(4), .width(64)) bitselector_4 (.in(register_2_q), .out(bitselector_4_out), .sel(4'b1111));
  BitSelector #(.width(64)) bitselector_5 (.in(fpcomparator_1_p4), .out(bitselector_5_out), .sel({6{1'b0}}));
  Comparator #(.mode("unsigned"), .width(4)) comparator_2 (.a(bitselector_3_out), .b(4'b0000));  // open: gt, eq, lt
  Comparator #(.mode("unsigned"), .width(4)) comparator_3 (
    .a(bitselector_3_out), .b(4'b0001), .eq(comparator_3_eq));  // open: gt, lt
  Comparator #(.mode("unsigned"), .width(4)) comparator_4 (
    .a(bitselector_3_out), .b(4'b0010), .eq(comparator_4_eq));  // open: gt, lt
  Counter #(.max('h1), .trigger("falling"), .width(1)) counter_1 (
    .count(comparator_4_eq), .Q(counter_1_q), .clk(clock_4_out), .clr(not_1_out));  // open: load, D, carry, up
  not not_1 (not_1_out, comparator_4_eq);
  Clock clock_4 (.out(clock_4_out));
  Comparator #(.mode("unsigned"), .width(4)) comparator_5 (
    .a(bitselector_3_out), .b(4'b0011), .eq(comparator_5_eq));  // open: gt, lt
  Counter #(.max('h3), .trigger("falling"), .width(2)) counter_2 (
    .count(comparator_5_eq), .Q(counter_2_q), .clk(clock_5_out), .clr(not_2_out));  // open: load, D, carry, up
  not not_2 (not_2_out, comparator_5_eq);
  Clock clock_5 (.out(clock_5_out));
  Comparator #(.mode("unsigned"), .width(4)) comparator_6 (
    .a(bitselector_3_out), .b(4'b0100), .eq(comparator_6_eq));  // open: gt, lt
  Counter #(.max('h3), .trigger("falling"), .width(2)) counter_3 (
    .count(comparator_6_eq), .Q(counter_3_q), .clk(clock_6_out), .clr(not_3_out));  // open: load, D, carry, up
  not not_3 (not_3_out, comparator_6_eq);
  Clock clock_6 (.out(clock_6_out));
  Comparator #(.mode("unsigned"), .width(4)) comparator_7 (
    .a(bitselector_3_out), .b(4'b0101), .eq(comparator_7_eq));  // open: gt, lt
  Multiplexer multiplexer_1 (
    .in0(comparator_8_eq), .in1(comparator_8_lt), .out(multiplexer_1_out), .sel(bitselector_1_out));
  Comparator #(.width(64)) comparator_8 (
    .a(fpcomparator_1_p4), .b({64{1'b0}}), .eq(comparator_8_eq), .lt(comparator_8_lt));  // open: gt
  Comparator #(.mode("unsigned"), .width(4)) comparator_9 (
    .a(bitselector_3_out), .b(4'b0110), .eq(comparator_9_eq));  // open: gt, lt
  Multiplexer multiplexer_2 (
    .in0(fpcomparator_1_p6), .in1(fpcomparator_1_p7), .out(multiplexer_2_out), .sel(bitselector_1_out));
  // FPComparator #(.fpwidth(64)) fpcomparator_1: pin names not known; wires that end beside it: register_2_q, bitselector_1_out, bitselector_3_out, fpcomparator_1_p4, {64{1'b0}}, fpcomparator_1_p6, fpcomparator_1_p7
  Register #(.width(64)) register_4 (
    .D(multiplexer_3_out), .en(demultiplexer_1_out2), .clk(clock_7_out), .Q(register_4_q));  // open: clr
  Clock clock_7 (.out(clock_7_out));
  Demultiplexer #(.select(4)) demultiplexer_1 (
    .out0(demultiplexer_1_out0), .out1(demultiplexer_1_out1), .out2(demultiplexer_1_out2),
    .out3(demultiplexer_1_out3), .in(or_2_out), .sel(bitselector_4_out));  // open: out4, out5, out6, out7, out8, out9, out10, out11, out12, out13, out14, out15
  and and_1 (and_1_out, bitselector_5_out, comparator_3_eq);
  or or_2 (or_2_out, comparator_10_eq, comparator_12_gt, and_2_out, and_3_out);
  Comparator #(.mode("unsigned"), .width(1)) comparator_10 (
    .a(counter_1_q), .b(1'b1), .eq(comparator_10_eq));  // open: gt, lt
  Comparator #(.mode("unsigned"), .width(2)) comparator_11 (
    .a(counter_2_q), .b(2'b01), .gt(comparator_11_gt), .eq(comparator_11_eq));  // open: lt
  Comparator #(.mode("unsigned"), .width(2)) comparator_12 (
    .a(counter_3_q), .b(2'b01), .gt(comparator_12_gt), .eq(comparator_12_eq));  // open: lt
  and and_2 (and_2_out, comparator_7_eq, multiplexer_1_out);
  assign or_3_out = 64'h1 | multiplexer_6_out;  // OR_Gate or_3, 64 bits wide
  and and_3 (and_3_out, comparator_9_eq, multiplexer_2_out);
  assign or_4_out = 64'h1 | multiplexer_6_out;  // OR_Gate or_4, 64 bits wide
  or or_5 (or_5_out, comparator_3_eq, or_2_out, comparator_11_gt, comparator_12_gt, comparator_7_eq, comparator_9_eq);
  Register #(.width(64)) register_5 (
    .D(multiplexer_3_out), .en(demultiplexer_1_out3), .clk(clock_8_out), .Q(register_5_q));  // open: clr
  Clock clock_8 (.out(clock_8_out));
  Multiplexer #(.select(4), .width(64)) multiplexer_3 (
    .in0(ram_1_dout), .in1(ram_1_dout), .in2(ram_1_dout), .in3(ram_1_dout), .in4(ram_1_dout), .in5(or_3_out),
    .in6(or_4_out), .out(multiplexer_3_out), .sel(bitselector_3_out));  // open: in7, in8, in9, in10, in11, in12, in13, in14, in15
  or or_6 (or_6_out, comparator_11_gt, comparator_12_gt);
  not not_4 (not_4_out, or_6_out);
  BitSelector #(.group(16), .width(64)) bitselector_6 (.in(multiplexer_6_out), .out(bitselector_6_out), .sel(2'b00));
  Register #(.width(64)) register_6 (
    .D(ram_1_dout), .en(comparator_11_eq), .clk(clock_9_out), .Q(register_6_q));  // open: clr
  Clock clock_9 (.out(clock_9_out));
  Register #(.width(1)) register_7 (.D(comparator_11_eq), .en(1'b1), .clk(clock_9_out), .Q(register_7_q));  // open: clr
  Register #(.width(64)) register_8 (
    .D(ram_1_dout), .en(comparator_12_eq), .clk(clock_10_out), .Q(register_8_q));  // open: clr
  Clock clock_10 (.out(clock_10_out));
  Register #(.width(1)) register_9 (
    .D(comparator_12_eq), .en(1'b1), .clk(clock_10_out), .Q(register_9_q));  // open: clr
  Counter #(.max('hffff), .width(16)) counter_4 (
    .load(and_1_out), .D(bitselector_6_out), .count(not_4_out), .Q(counter_4_q), .clk(clock_11_out));  // open: carry, up, clr
  Clock clock_11 (.out(clock_11_out));
  Multiplexer #(.width(16)) multiplexer_4 (
    .in0(counter_4_q), .in1(bitselector_7_out), .out(multiplexer_4_out), .sel(register_7_q));
  BitSelector #(.group(16), .width(64)) bitselector_7 (.in(register_6_q), .out(bitselector_7_out), .sel(2'b00));
  Multiplexer #(.width(16)) multiplexer_5 (
    .in0(counter_4_q), .in1(bitselector_8_out), .out(multiplexer_5_out), .sel(register_9_q));
  BitSelector #(.group(16), .width(64)) bitselector_8 (.in(register_8_q), .out(bitselector_8_out), .sel(2'b00));
  Multiplexer #(.select(4), .width(64)) multiplexer_6 (
    .in0(register_1_q), .in1(register_3_q), .in2(register_4_q), .in3(register_5_q), .out(multiplexer_6_out),
    .sel(bitselector_4_out));  // open: in4, in5, in6, in7, in8, in9, in10, in11, in12, in13, in14, in15
  Multiplexer #(.select(4), .width(64)) multiplexer_7 (
    .in0(register_1_q), .in1(register_3_q), .in2(register_4_q), .in3(register_5_q), .out(fpcomparator_1_p4),
    .sel(bitselector_2_out));  // open: in4, in5, in6, in7, in8, in9, in10, in11, in12, in13, in14, in15
  Multiplexer #(.select(4), .width(16)) multiplexer_8 (
    .in0(counter_4_q), .in1(counter_4_q), .in2(counter_4_q), .in3(multiplexer_4_out),
    .in4(multiplexer_5_out), .in5(counter_4_q), .in6(counter_4_q), .out(multiplexer_8_out),
    .sel(bitselector_3_out));  // open: in7, in8, in9, in10, in11, in12, in13, in14, in15
  Clock clock_12 (.out(clock_12_out));
  Multiplexer #(.select(4)) multiplexer_9 (
    .in0(1'b0), .in1(1'b0), .in2(1'b0), .in3(comparator_11_gt), .in4(1'b0), .in5(1'b0), .in6(1'b0),
    .out(multiplexer_9_out), .sel(bitselector_3_out));  // open: in7, in8, in9, in10, in11, in12, in13, in14, in15
  Multiplexer #(.select(4), .width(64)) multiplexer_10 (
    .in0({64{1'b0}}), .in1({64{1'b0}}), .in2({64{1'b0}}), .in3(multiplexer_6_out), .in4({64{1'b0}}),
    .in5({64{1'b0}}), .in6({64{1'b0}}), .out(multiplexer_10_out), .sel(bitselector_3_out));  // open: in7, in8, in9, in10, in11, in12, in13, in14, in15
  RAM #(.addrWidth(16), .dataWidth(64), .enables("line"), .\type ("nonvolatile")) ram_1 (
    .addr(multiplexer_8_out), .we(multiplexer_9_out), .clk(clock_12_out), .din(multiplexer_10_out),
    .dout(ram_1_dout));
endmodule
